# Fritzing sketch Untitled Sketch 2 (saved by Fritzing 0.9.4)
breadboards: 1

parts:
  Part1 = Arduino Mega ADK (Rev3)
  U1 = Module 4 Relais 5V [package="Module 4 Relais 5V"]
  2_Channel_Relay1 = 2 Channel Power Relay
  Part2 = FC-28 Soil Hygrometer Module
  Part3 = FC-28 Soil Hygrometer Module - Probe
  DHT1 = DHT11 Humitidy and Temperature Sensor
  Part4 = Bluetooth HM-10
  U2 = NodeMCU V1.0

nets:
  N1: Part1.A0, Part2.AO
  N2: Part1.D19/RX1, Part4.TXD
  N3: Part1.D18/TX1, Part4.RXD
  N4: Part1.D17/RX2, U2.TX
  N5: Part1.D16/TX2, U2.RX
  GND: Part1.GND, U1.GND, 2_Channel_Relay1.GND, Part2.GND, DHT1.GND, Part4.GND, U2.GND
  3V3: Part1.3V3, Part4.VCC, U2.3V3
  VCC: Part1.5V, U1.VCC, 2_Channel_Relay1.VCC, Part2.VCC, DHT1.VDD
  N6: Part1.D2_PWM, U1.IN4
  N7: Part1.D3_PWM, U1.IN3
  N8: Part1.D4_PWM, U1.IN2
  N9: Part1.D5_PWM, U1.IN1
  N10: Part1.D6_PWM, 2_Channel_Relay1.IN2
  N11: Part1.D7_PWM, 2_Channel_Relay1.IN1
  N12: Part1.D23, DHT1.DATA
  N13: Part2.POS, Part3.POS
  N14: Part2.NEG, Part3.NEG

custom parts:
  Module 4 Relais 5V: Module 4 Relais 5V 4x SPD-06VDC-SD-C
  2 Channel Power Relay: A 2 channel power relay. The module operates at 5V.
  FC-28 Soil Hygrometer Module: The FC-28 is a soil hygrometer module that uses the Texas Instruments LM393 comparator chip to provide an analog measurement of soil humidity. The digital output is high when soil moisture is over a certain threshold, as determined by adjusting the potentiometer.
  FC-28 Soil Hygrometer Module - Probe: The FC-28 is a soil hygrometer module that uses the Texas Instruments LM393 comparator chip to provide an analog measurement of soil humidity.
  DHT11 Humitidy and Temperature Sensor: DHT11 Humidity and Temperature Sensor
  NodeMCU V1.0: ESP8266 based NodeMCU
